// Logisim project lab2_3.circ as structural Verilog: 1 circuit, main circuit main
module main (
  input  in_1,
  input  in_2,
  input  in_3,
  input  in_4,
  input  in_5,
  input  in_6,
  input  in_7,
  input  in_8,
  input  in_9,
  input  in_10,
  input  in_11,
  input  in_12,
  output out_13,
  output out_14,
  output out_15,
  output out_16,
  output out_17,
  output out_18,
  output out_19
);

  wire and_1_out, and_2_out, and_3_out, and_4_out, and_5_out, and_6_out, and_7_out, and_8_out, and_9_out,
       and_10_out, or_2_out, or_3_out, or_4_out, xor_1_out, xor_2_out, xor_3_out, xor_4_out, xor_5_out;

  xor xor_1 (xor_1_out, in_11, in_12);
  and and_1 (and_1_out, in_11, in_12);
  xor xor_2 (xor_2_out, in_2, in_3);
  and and_2 (and_2_out, in_2, in_3);
  xor xor_3 (xor_3_out, in_5, in_6);
  and and_3 (and_3_out, in_5, in_6);
  xor xor_4 (xor_4_out, in_7, in_8);
  and and_4 (and_4_out, in_7, in_8);
  xor xor_5 (xor_5_out, in_9, in_10);
  and and_5 (and_5_out, in_9, in_10);
  and and_6 (and_6_out, xor_2_out, in_1);
  xor xor_6 (out_15, in_4, xor_3_out);
  and and_7 (and_7_out, xor_3_out, in_4);
  xor xor_7 (out_16, or_2_out, xor_4_out);
  and and_8 (and_8_out, xor_4_out, or_2_out);
  xor xor_8 (out_17, or_3_out, xor_5_out);
  and and_9 (and_9_out, xor_5_out, or_3_out);
  xor xor_9 (out_18, or_4_out, xor_1_out);
  and and_10 (and_10_out, xor_1_out, or_4_out);
  xor xor_10 (out_13, in_1, xor_2_out);
  or or_1 (out_14, and_6_out, and_2_out);
  or or_2 (or_2_out, and_7_out, and_3_out);
  or or_3 (or_3_out, and_8_out, and_4_out);
  or or_4 (or_4_out, and_9_out, and_5_out);
  or or_5 (out_19, and_10_out, and_1_out);
endmodule
