// Logisim project lab2_5.circ as structural Verilog: 1 circuit, main circuit main
module main (
  input  in_1,
  input  in_2,
  input  in_3,
  input  in_4,
  input  [2:0] in_5,
  input  in_6,
  input  in_7,
  input  in_8,
  input  in_9,
  input  [2:0] in_10,
  input  in_11,
  input  in_12,
  input  in_13,
  input  in_14,
  input  [2:0] in_15,
  input  in_16,
  input  in_17,
  input  in_18,
  input  in_19,
  input  [2:0] in_20,
  input  in_21,
  input  in_22,
  input  in_23,
  input  in_24,
  input  [2:0] in_25,
  input  in_26,
  input  in_27,
  input  in_28,
  input  in_29,
  input  [2:0] in_30,
  input  in_31,
  input  in_32,
  input  in_33,
  input  in_34,
  input  [2:0] in_35,
  input  in_36,
  input  in_37,
  input  in_38,
  input  in_39,
  input  [2:0] in_40,
  input  in_41,
  input  in_42,
  output out_43,
  output out_44,
  output out_45,
  output out_46,
  output out_47,
  output out_48,
  output out_49,
  output out_50,
  output out_51,
  output out_52,
  output out_53,
  output out_54
);

  wire adder_1_cout, adder_1_out, adder_2_out, adder_3_cout, adder_3_out, adder_4_cout, adder_4_out,
       adder_5_cout, adder_5_out, adder_6_cout, adder_6_out, adder_7_cout, adder_7_out, adder_8_cout,
       adder_8_out, comparator_1_eq, comparator_1_gt, comparator_1_lt, comparator_2_eq, comparator_2_gt,
       comparator_2_lt, comparator_3_eq, comparator_3_gt, comparator_3_lt, comparator_4_eq, comparator_4_gt,
       comparator_4_lt, comparator_5_eq, comparator_5_gt, comparator_5_lt, comparator_6_eq, comparator_6_gt,
       comparator_6_lt, comparator_7_eq, comparator_7_gt, comparator_7_lt, comparator_8_eq, comparator_8_gt,
       comparator_8_lt, divider_1_out, divider_1_rem, divider_2_out, divider_3_out, divider_3_rem,
       divider_4_out, divider_4_rem, divider_5_out, divider_5_rem, divider_6_out, divider_6_rem,
       divider_7_out, divider_7_rem, divider_8_out, divider_8_rem, multiplexer_1_out, multiplexer_2_out,
       multiplexer_3_out, multiplexer_4_out, multiplexer_5_out, multiplexer_6_out, multiplexer_7_out,
       multiplexer_8_out, multiplexer_9_out, multiplexer_10_out, multiplexer_11_out, multiplexer_12_out,
       multiplexer_13_out, multiplexer_14_out, multiplexer_15_out, multiplexer_16_out, multiplier_1_cout,
       multiplier_1_out, multiplier_2_out, multiplier_3_cout, multiplier_3_out, multiplier_4_cout,
       multiplier_4_out, multiplier_5_cout, multiplier_5_out, multiplier_6_cout, multiplier_6_out,
       multiplier_7_cout, multiplier_7_out, multiplier_8_cout, multiplier_8_out, not_1_out, not_2_out,
       not_3_out, not_4_out, not_5_out, not_6_out, not_7_out, not_8_out, not_9_out, not_10_out, not_11_out,
       not_12_out, not_13_out, not_14_out, not_15_out, not_16_out, subtractor_1_bout, subtractor_1_out,
       subtractor_2_out, subtractor_3_bout, subtractor_3_out, subtractor_4_bout, subtractor_4_out,
       subtractor_5_bout, subtractor_5_out, subtractor_6_bout, subtractor_6_out, subtractor_7_bout,
       subtractor_7_out, subtractor_8_bout, subtractor_8_out, xor_1_out, xor_2_out, xor_3_out, xor_4_out,
       xor_5_out, xor_6_out, xor_7_out, xor_8_out;

  not not_1 (not_1_out, in_42);
  Multiplexer multiplexer_1 (.in0(in_6), .in1(not_2_out), .out(multiplexer_1_out), .sel(in_3));
  not not_2 (not_2_out, in_6);
  Multiplexer multiplexer_2 (.in0(in_7), .in1(not_3_out), .out(multiplexer_2_out), .sel(in_4));
  not not_3 (not_3_out, in_7);
  not not_4 (not_4_out, in_11);
  not not_5 (not_5_out, in_12);
  not not_6 (not_6_out, in_16);
  not not_7 (not_7_out, in_17);
  not not_8 (not_8_out, in_21);
  not not_9 (not_9_out, in_22);
  not not_10 (not_10_out, in_26);
  Multiplexer multiplexer_3 (.in0(in_27), .in1(not_11_out), .out(multiplexer_3_out), .sel(in_24));
  not not_11 (not_11_out, in_27);
  Multiplexer multiplexer_4 (.in0(in_31), .in1(not_12_out), .out(multiplexer_4_out), .sel(in_28));
  not not_12 (not_12_out, in_31);
  Multiplexer multiplexer_5 (.in0(in_32), .in1(not_13_out), .out(multiplexer_5_out), .sel(in_29));
  not not_13 (not_13_out, in_32);
  Multiplexer multiplexer_6 (.in0(in_36), .in1(not_14_out), .out(multiplexer_6_out), .sel(in_33));
  not not_14 (not_14_out, in_36);
  Multiplexer multiplexer_7 (.in0(in_37), .in1(not_15_out), .out(multiplexer_7_out), .sel(in_34));
  not not_15 (not_15_out, in_37);
  Multiplexer multiplexer_8 (.in0(in_41), .in1(not_16_out), .out(multiplexer_8_out), .sel(in_38));
  not not_16 (not_16_out, in_41);
  Multiplexer multiplexer_9 (.in0(in_42), .in1(not_1_out), .out(multiplexer_9_out), .sel(in_39));
  Multiplexer multiplexer_10 (.in0(in_11), .in1(not_4_out), .out(multiplexer_10_out), .sel(in_8));
  Multiplexer multiplexer_11 (.in0(in_12), .in1(not_5_out), .out(multiplexer_11_out), .sel(in_9));
  Multiplexer multiplexer_12 (.in0(in_16), .in1(not_6_out), .out(multiplexer_12_out), .sel(in_13));
  Multiplexer multiplexer_13 (.in0(in_17), .in1(not_7_out), .out(multiplexer_13_out), .sel(in_14));
  Multiplexer multiplexer_14 (.in0(in_21), .in1(not_8_out), .out(multiplexer_14_out), .sel(in_18));
  Multiplexer multiplexer_15 (.in0(in_22), .in1(not_9_out), .out(multiplexer_15_out), .sel(in_19));
  Multiplexer multiplexer_16 (.in0(in_26), .in1(not_10_out), .out(multiplexer_16_out), .sel(in_23));
  xor xor_1 (xor_1_out, multiplexer_1_out, multiplexer_2_out);
  Comparator #(.width(1)) comparator_1 (
    .a(multiplexer_1_out), .b(multiplexer_2_out), .gt(comparator_1_gt), .eq(comparator_1_eq),
    .lt(comparator_1_lt));
  xor xor_2 (xor_2_out, multiplexer_4_out, multiplexer_5_out);
  Comparator #(.width(1)) comparator_2 (
    .a(multiplexer_4_out), .b(multiplexer_5_out), .gt(comparator_2_gt), .eq(comparator_2_eq),
    .lt(comparator_2_lt));
  Adder #(.width(1)) adder_1 (
    .a(multiplexer_6_out), .b(multiplexer_7_out), .out(adder_1_out), .cin(adder_8_cout), .cout(adder_1_cout));
  Subtractor #(.width(1)) subtractor_1 (
    .a(multiplexer_6_out), .b(multiplexer_7_out), .out(subtractor_1_out), .bin(subtractor_8_bout),
    .bout(subtractor_1_bout));
  Multiplier #(.width(1)) multiplier_1 (
    .a(multiplexer_6_out), .b(multiplexer_7_out), .out(multiplier_1_out), .cin(multiplier_8_cout),
    .cout(multiplier_1_cout));
  Divider #(.width(1)) divider_1 (
    .a(multiplexer_6_out), .b(multiplexer_7_out), .out(divider_1_out), .upper(divider_8_rem),
    .rem(divider_1_rem));
  xor xor_3 (xor_3_out, multiplexer_6_out, multiplexer_7_out);
  Comparator #(.width(1)) comparator_3 (
    .a(multiplexer_6_out), .b(multiplexer_7_out), .gt(comparator_3_gt), .eq(comparator_3_eq),
    .lt(comparator_3_lt));
  Adder #(.width(1)) adder_2 (
    .a(multiplexer_8_out), .b(multiplexer_9_out), .out(adder_2_out), .cin(adder_1_cout), .cout(out_51));
  Subtractor #(.width(1)) subtractor_2 (
    .a(multiplexer_8_out), .b(multiplexer_9_out), .out(subtractor_2_out), .bin(subtractor_1_bout),
    .bout(out_52));
  Multiplier #(.width(1)) multiplier_2 (
    .a(multiplexer_8_out), .b(multiplexer_9_out), .out(multiplier_2_out), .cin(multiplier_1_cout),
    .cout(out_53));
  Divider #(.width(1)) divider_2 (
    .a(multiplexer_8_out), .b(multiplexer_9_out), .out(divider_2_out), .upper(divider_1_rem), .rem(out_54));
  xor xor_4 (xor_4_out, multiplexer_8_out, multiplexer_9_out);
  Comparator #(.width(1)) comparator_4 (
    .a(multiplexer_8_out), .b(multiplexer_9_out), .gt(comparator_4_gt), .eq(comparator_4_eq),
    .lt(comparator_4_lt));
  Adder #(.width(1)) adder_3 (
    .a(multiplexer_1_out), .b(multiplexer_2_out), .out(adder_3_out), .cin(in_1), .cout(adder_3_cout));
  Subtractor #(.width(1)) subtractor_3 (
    .a(multiplexer_1_out), .b(multiplexer_2_out), .out(subtractor_3_out), .bin(in_1), .bout(subtractor_3_bout));
  Multiplier #(.width(1)) multiplier_3 (
    .a(multiplexer_1_out), .b(multiplexer_2_out), .out(multiplier_3_out), .cin(in_2), .cout(multiplier_3_cout));
  Divider #(.width(1)) divider_3 (
    .a(multiplexer_1_out), .b(multiplexer_2_out), .out(divider_3_out), .upper(in_2), .rem(divider_3_rem));
  Adder #(.width(1)) adder_4 (
    .a(multiplexer_10_out), .b(multiplexer_11_out), .out(adder_4_out), .cin(adder_3_cout), .cout(adder_4_cout));
  Subtractor #(.width(1)) subtractor_4 (
    .a(multiplexer_10_out), .b(multiplexer_11_out), .out(subtractor_4_out), .bin(subtractor_3_bout),
    .bout(subtractor_4_bout));
  Multiplier #(.width(1)) multiplier_4 (
    .a(multiplexer_10_out), .b(multiplexer_11_out), .out(multiplier_4_out), .cin(multiplier_3_cout),
    .cout(multiplier_4_cout));
  Divider #(.width(1)) divider_4 (
    .a(multiplexer_10_out), .b(multiplexer_11_out), .out(divider_4_out), .upper(divider_3_rem),
    .rem(divider_4_rem));
  xor xor_5 (xor_5_out, multiplexer_10_out, multiplexer_11_out);
  Comparator #(.width(1)) comparator_5 (
    .a(multiplexer_10_out), .b(multiplexer_11_out), .gt(comparator_5_gt), .eq(comparator_5_eq),
    .lt(comparator_5_lt));
  Adder #(.width(1)) adder_5 (
    .a(multiplexer_12_out), .b(multiplexer_13_out), .out(adder_5_out), .cin(adder_4_cout), .cout(adder_5_cout));
  Subtractor #(.width(1)) subtractor_5 (
    .a(multiplexer_12_out), .b(multiplexer_13_out), .out(subtractor_5_out), .bin(subtractor_4_bout),
    .bout(subtractor_5_bout));
  Multiplier #(.width(1)) multiplier_5 (
    .a(multiplexer_12_out), .b(multiplexer_13_out), .out(multiplier_5_out), .cin(multiplier_4_cout),
    .cout(multiplier_5_cout));
  Divider #(.width(1)) divider_5 (
    .a(multiplexer_12_out), .b(multiplexer_13_out), .out(divider_5_out), .upper(divider_4_rem),
    .rem(divider_5_rem));
  xor xor_6 (xor_6_out, multiplexer_12_out, multiplexer_13_out);
  Comparator #(.width(1)) comparator_6 (
    .a(multiplexer_12_out), .b(multiplexer_13_out), .gt(comparator_6_gt), .eq(comparator_6_eq),
    .lt(comparator_6_lt));
  Adder #(.width(1)) adder_6 (
    .a(multiplexer_14_out), .b(multiplexer_15_out), .out(adder_6_out), .cin(adder_5_cout), .cout(adder_6_cout));
  Subtractor #(.width(1)) subtractor_6 (
    .a(multiplexer_14_out), .b(multiplexer_15_out), .out(subtractor_6_out), .bin(subtractor_5_bout),
    .bout(subtractor_6_bout));
  Multiplier #(.width(1)) multiplier_6 (
    .a(multiplexer_14_out), .b(multiplexer_15_out), .out(multiplier_6_out), .cin(multiplier_5_cout),
    .cout(multiplier_6_cout));
  Divider #(.width(1)) divider_6 (
    .a(multiplexer_14_out), .b(multiplexer_15_out), .out(divider_6_out), .upper(divider_5_rem),
    .rem(divider_6_rem));
  xor xor_7 (xor_7_out, multiplexer_14_out, multiplexer_15_out);
  Comparator #(.width(1)) comparator_7 (
    .a(multiplexer_14_out), .b(multiplexer_15_out), .gt(comparator_7_gt), .eq(comparator_7_eq),
    .lt(comparator_7_lt));
  Adder #(.width(1)) adder_7 (
    .a(multiplexer_16_out), .b(multiplexer_3_out), .out(adder_7_out), .cin(adder_6_cout), .cout(adder_7_cout));
  Subtractor #(.width(1)) subtractor_7 (
    .a(multiplexer_16_out), .b(multiplexer_3_out), .out(subtractor_7_out), .bin(subtractor_6_bout),
    .bout(subtractor_7_bout));
  Multiplier #(.width(1)) multiplier_7 (
    .a(multiplexer_16_out), .b(multiplexer_3_out), .out(multiplier_7_out), .cin(multiplier_6_cout),
    .cout(multiplier_7_cout));
  Divider #(.width(1)) divider_7 (
    .a(multiplexer_16_out), .b(multiplexer_3_out), .out(divider_7_out), .upper(divider_6_rem),
    .rem(divider_7_rem));
  xor xor_8 (xor_8_out, multiplexer_16_out, multiplexer_3_out);
  Comparator #(.width(1)) comparator_8 (
    .a(multiplexer_16_out), .b(multiplexer_3_out), .gt(comparator_8_gt), .eq(comparator_8_eq),
    .lt(comparator_8_lt));
  Adder #(.width(1)) adder_8 (
    .a(multiplexer_4_out), .b(multiplexer_5_out), .out(adder_8_out), .cin(adder_7_cout), .cout(adder_8_cout));
  Subtractor #(.width(1)) subtractor_8 (
    .a(multiplexer_4_out), .b(multiplexer_5_out), .out(subtractor_8_out), .bin(subtractor_7_bout),
    .bout(subtractor_8_bout));
  Multiplier #(.width(1)) multiplier_8 (
    .a(multiplexer_4_out), .b(multiplexer_5_out), .out(multiplier_8_out), .cin(multiplier_7_cout),
    .cout(multiplier_8_cout));
  Divider #(.width(1)) divider_8 (
    .a(multiplexer_4_out), .b(multiplexer_5_out), .out(divider_8_out), .upper(divider_7_rem),
    .rem(divider_8_rem));
  Multiplexer #(.select(3)) multiplexer_17 (
    .in0(adder_3_out), .in1(subtractor_3_out), .in2(multiplier_3_out), .in3(divider_3_out), .in4(xor_1_out),
    .in5(comparator_1_gt), .in6(comparator_1_eq), .in7(comparator_1_lt), .out(out_43), .sel(in_5));
  Multiplexer #(.select(3)) multiplexer_18 (
    .in0(adder_4_out), .in1(subtractor_4_out), .in2(multiplier_4_out), .in3(divider_4_out), .in4(xor_5_out),
    .in5(comparator_5_gt), .in6(comparator_5_eq), .in7(comparator_5_lt), .out(out_44), .sel(in_10));
  Multiplexer #(.select(3)) multiplexer_19 (
    .in0(adder_5_out), .in1(subtractor_5_out), .in2(multiplier_5_out), .in3(divider_5_out), .in4(xor_6_out),
    .in5(comparator_6_gt), .in6(comparator_6_eq), .in7(comparator_6_lt), .out(out_45), .sel(in_15));
  Multiplexer #(.select(3)) multiplexer_20 (
    .in0(adder_6_out), .in1(subtractor_6_out), .in2(multiplier_6_out), .in3(divider_6_out), .in4(xor_7_out),
    .in5(comparator_7_gt), .in6(comparator_7_eq), .in7(comparator_7_lt), .out(out_46), .sel(in_20));
  Multiplexer #(.select(3)) multiplexer_21 (
    .in0(adder_7_out), .in1(subtractor_7_out), .in2(multiplier_7_out), .in3(divider_7_out), .in4(xor_8_out),
    .in5(comparator_8_gt), .in6(comparator_8_eq), .in7(comparator_8_lt), .out(out_47), .sel(in_25));
  Multiplexer #(.select(3)) multiplexer_22 (
    .in0(adder_8_out), .in1(subtractor_8_out), .in2(multiplier_8_out), .in3(divider_8_out), .in4(xor_2_out),
    .in5(comparator_2_gt), .in6(comparator_2_eq), .in7(comparator_2_lt), .out(out_48), .sel(in_30));
  Multiplexer #(.select(3)) multiplexer_23 (
    .in0(adder_1_out), .in1(subtractor_1_out), .in2(multiplier_1_out), .in3(divider_1_out), .in4(xor_3_out),
    .in5(comparator_3_gt), .in6(comparator_3_eq), .in7(comparator_3_lt), .out(out_49), .sel(in_35));
  Multiplexer #(.select(3)) multiplexer_24 (
    .in0(adder_2_out), .in1(subtractor_2_out), .in2(multiplier_2_out), .in3(divider_2_out), .in4(xor_4_out),
    .in5(comparator_4_gt), .in6(comparator_4_eq), .in7(comparator_4_lt), .out(out_50), .sel(in_40));
endmodule
